# Fritzing sketch Schaltplan (saved by Fritzing 0.9.3b)
breadboards: 2

parts:
  U1 = ESP32-38PinWide [part_number=ESP32-38PinWide]
  BB_PWR1 = Toaster Bread Board Dual Supply [package="DIP (Dual Inline) [THT]"]
  F1 = Fan - Ventilador [package=THT]
  R1 = Resistor [tolerance=±5% resistance=220 package=THT]
  WATER_PUMP1 = water pump/motor  # not connected
  U2 = TRANSISTOR_NPN_2 [package=to-92]
  U3 = TRANSISTOR_NPN_2 [package=to-92]
  R2 = Resistor [tolerance=±5% resistance=220 package=THT]
  U4 = WS2812 RGB LED strip
  C1 = Electrolytic Capacitor [capacitance=1000µF package="300 mil [THT, electrolytic]"]
  R3 = Resistor [tolerance=±5% resistance=220 package=THT]
  Bauteil1 = Soil Moisture Sensor
  DHT1 = Humidity and Temperature Sensor DHT11

nets:
  N1: U1.GPIO32, Bauteil1.SIG
  N2: U1.GPIO33, R3.Pin_0
  N3: U1.GPIO18, R2.Pin_0
  N4: U1.GPIO21, DHT1.Data-signal
  N5: U1.GPIO23, R1.Pin_0
  GND: U1.GND, BB_PWR1.VS2, U4.GND, C1.-
  VCC: BB_PWR1.VO1, F1.5V, Bauteil1.VCC, DHT1.Vcc
  GND_2: BB_PWR1.GND, U2.E, U3.C, Bauteil1.GND, DHT1.GND_1
  N6: BB_PWR1.VS1, U4.VCC, C1.+
  N7: F1.GND, U2.C
  N8: R1.Pin_1, U2.B
  N9: U3.B, R2.Pin_1
  N10: U4.DIN, R3.Pin_1

custom parts:
  ESP32-38PinWide: Generic 38-Pin ESP32 with wide format (only access to one side of pins on a breadboard) based on Stephen Lilley's HiLetgo ESP-WROOM-32 ESP32 ESP-32S Development Board.
  Toaster Bread Board Dual Supply: Toaster is dual output USB step up power supply module designed to fit snuggly into a breadboard. It is powered by a single 5V USB port or charger and outputs three voltages simultaneously, these being 3.3V, 5V and a variable supply which is capable of 5V to 16V.
  Fan - Ventilador: Ventilador de 2 pines, se encuentra comunmente en computadoras de escritorio
  water pump/motor: WATER PUMP BY ARDUBLOCKTR
  WS2812 RGB LED strip: WS2812 strip
  Humidity and Temperature Sensor DHT11: Digital relative humidity & temperature sensor DHT11
